# Fritzing sketch exDotMatrixS_Circuit (saved by Fritzing 0.9.3b)

parts:
  Disp1 = LBT2088AH [part_number=LBT2088AH]
  부품1 = Arduino Due (Rev2b)

nets:
  N1: Disp1.pin1, 부품1.D30
  N2: Disp1.pin2, 부품1.D32
  N3: Disp1.pin_3, 부품1.D34
  N4: Disp1.pin_4, 부품1.D36
  N5: Disp1.pin_5, 부품1.D38
  N6: Disp1.pin_6, 부품1.D40
  N7: Disp1.pin_7, 부품1.D42
  N8: Disp1.pin_8, 부품1.D44
  N9: Disp1.pin_9, 부품1.D31
  N10: Disp1.pin_10, 부품1.D33
  N11: Disp1.pin_11, 부품1.D35
  N12: Disp1.pin_12, 부품1.D37
  N13: Disp1.pin_13, 부품1.D39
  N14: Disp1.pin_14, 부품1.D41
  N15: Disp1.pin_15, 부품1.D43
  N16: Disp1.pin_16, 부품1.D45
