# Fritzing sketch exDutyMotorSpeed_Circuit (saved by Fritzing 0.9.3b)
breadboards: 1

parts:
  부품1 = Arduino Due (Rev2b)
  S1 = H-Bridge with L298N
  M1 = DC Motor

nets:
  5V: 부품1.5V, S1.5V
  GND: 부품1.GND, S1.GND
  N1: 부품1.D2_PWM, S1.ENA
  N2: 부품1.D30, S1.IN1
  N3: 부품1.D32, S1.IN2
  N4: S1.M1-01, M1.pin_2
  N5: S1.M1-02, M1.pin_1
  N6: S1.M2-01, S1.M2-02, S1.ENA-5V

custom parts:
  H-Bridge with L298N: h-bridge
